// Logisim project prelim3.circ as structural Verilog: 1 circuit, main circuit main
module main (
  input  [4:0] in_1,
  output out_2
);

  wire and_1_out, and_2_out, not_1_out, not_2_out, not_3_out, not_4_out;

  and and_1 (and_1_out, in_1[1], not_1_out);
  not not_1 (not_1_out, in_1[0]);
  not not_2 (not_2_out, in_1[1]);
  not not_3 (not_3_out, and_2_out);
  not not_4 (not_4_out, and_1_out);
  and and_2 (and_2_out, not_2_out, in_1[0]);
  Multiplexer #(.select(3)) multiplexer_1 (
    .in0(in_1[1]), .in1(and_1_out), .in2(and_2_out), .in3(and_2_out), .in4(not_3_out), .in5(and_2_out),
    .in6(not_2_out), .in7(not_4_out), .out(out_2), .sel(in_1[4:2]));  // open: en
endmodule
