// Logisim project pre4.circ as structural Verilog: 1 circuit, main circuit main
module main (
  input  in_1,
  input  in_2,
  output out_3,
  output out_4,
  output out_5,
  output out_6
);

  wire clock_1_out, d_ff_1_q, d_ff_2_qn, nand_1_out, nand_2_out, nand_3_out;

  Clock clock_1 (.out(clock_1_out));
  D_Flip_Flop d_ff_1 (.clk(clock_1_out), .D(in_1), .Q(d_ff_1_q));  // open: Qn, preset, en, reset
  D_Flip_Flop d_ff_2 (.clk(clock_1_out), .D(in_2), .Q(out_6), .Qn(d_ff_2_qn));  // open: preset, en, reset
  nand nand_1 (nand_1_out, d_ff_1_q, out_6);
  and and_1 (out_3, out_6, d_ff_1_q);
  and and_2 (out_4, d_ff_1_q, d_ff_2_qn);
  nand nand_2 (nand_2_out, d_ff_1_q, nand_1_out);
  nand nand_3 (nand_3_out, nand_1_out, out_6);
  nand nand_4 (out_5, nand_2_out, nand_3_out);
endmodule
