// Logisim project circuit.circ as structural Verilog: 1 circuit, main circuit main
module main (
  input  in_1,
  input  in_2,
  output out_3
);

  wire and_1_out, and_2_out, and_3_out, and_4_out, and_5_out, and_6_out, and_7_out, and_8_out, and_9_out,
       and_10_out, clock_1_out, not_1_out, not_2_out, not_3_out, not_4_out, not_5_out, not_6_out, not_7_out,
       not_8_out, not_9_out, not_10_out, not_11_out, not_12_out, not_13_out, not_14_out, not_15_out;
  wire [2:0] or_1_out, register_1_q;

  not not_1 (not_1_out, register_1_q[2]);
  not not_2 (not_2_out, register_1_q[1]);
  not not_3 (not_3_out, register_1_q[0]);
  not not_4 (not_4_out, register_1_q[2]);
  not not_5 (not_5_out, register_1_q[1]);
  not not_6 (not_6_out, register_1_q[2]);
  not not_7 (not_7_out, register_1_q[0]);
  not not_8 (not_8_out, in_1);
  not not_9 (not_9_out, register_1_q[1]);
  not not_10 (not_10_out, register_1_q[2]);
  and and_1 (and_1_out, not_10_out, not_11_out, not_12_out);
  not not_11 (not_11_out, register_1_q[1]);
  not not_12 (not_12_out, register_1_q[0]);
  not not_13 (not_13_out, register_1_q[0]);
  and and_2 (and_2_out, in_1, not_13_out, not_14_out);
  not not_14 (not_14_out, register_1_q[2]);
  not not_15 (not_15_out, register_1_q[1]);
  and and_3 (and_3_out, not_15_out, in_1);
  and and_4 (and_4_out, not_1_out, not_2_out, register_1_q[0]);
  and and_5 (and_5_out, not_1_out, register_1_q[1], not_3_out);
  and and_6 (and_6_out, not_1_out, not_3_out, in_1);
  and and_7 (and_7_out, register_1_q[0], register_1_q[1], not_4_out, in_1);
  and and_8 (and_8_out, not_5_out, register_1_q[2], in_1);
  and and_9 (and_9_out, not_6_out, register_1_q[1], not_7_out, not_8_out);
  and and_10 (and_10_out, register_1_q[2], not_9_out, register_1_q[0], in_1);
  or or_1 (or_1_out[0], and_1_out, and_2_out, and_3_out);
  or or_2 (or_1_out[1], and_4_out, and_5_out, and_6_out);
  or or_3 (or_1_out[2], and_7_out, and_8_out);
  or or_4 (out_3, and_9_out, and_10_out);
  Register #(.width(3)) register_1 (.D(or_1_out), .Q(register_1_q), .clk(clock_1_out), .clr(in_2));  // open: en
  Clock clock_1 (.out(clock_1_out));

  // Notes on the sheet:
  //   s2
  //   s2
  //   n0
endmodule
